// Logisim project 4-bit-memory.circ as structural Verilog: 2 circuits, main circuit main
module main (
  input  Enable,
  input  RESET,
  input  [3:0] Input,
  input  [4:0] Address,
  output [3:0] Output
);

  wire Clock_out;

  Clock Clock (.out(Clock_out));
  Memory memory_1 (
    .clock(Clock_out), .Enable(Enable), .RESET(RESET), .Input(Input), .Address(Address), .Output(Output));

  // Notes on the sheet:
  //   5 bit address
  //   location to store data
endmodule

// RAM
module Memory (
  input  clock,
  input  Enable,
  input  RESET,
  input  [3:0] Input,
  input  [4:0] Address,
  output [3:0] Output
);

  wire decoder_1_out0, decoder_1_out1, decoder_1_out2, decoder_1_out3, decoder_1_out4, decoder_1_out5,
       decoder_1_out6, decoder_1_out7, decoder_1_out8, decoder_1_out9, decoder_1_out10, decoder_1_out11,
       decoder_1_out12, decoder_1_out13, decoder_1_out14, decoder_1_out15, decoder_1_out16, decoder_1_out17,
       decoder_1_out18, decoder_1_out19, decoder_1_out20, decoder_1_out21, decoder_1_out22, decoder_1_out23,
       decoder_1_out24, decoder_1_out25, decoder_1_out26, decoder_1_out27, decoder_1_out28, decoder_1_out29,
       decoder_1_out30, decoder_1_out31;
  wire [3:0] d_ff_97_q, d_ff_98_q, d_ff_99_q, d_ff_100_q, d_ff_101_q, d_ff_102_q, d_ff_103_q, d_ff_104_q,
       d_ff_105_q, d_ff_106_q, d_ff_107_q, d_ff_108_q, d_ff_109_q, d_ff_110_q, d_ff_111_q, d_ff_112_q,
       d_ff_113_q, d_ff_114_q, d_ff_115_q, d_ff_116_q, d_ff_117_q, d_ff_118_q, d_ff_119_q, d_ff_120_q,
       d_ff_121_q, d_ff_122_q, d_ff_123_q, d_ff_124_q, d_ff_125_q, d_ff_126_q, d_ff_127_q, d_ff_128_q,
       undriven;

  Decoder #(.select(5)) decoder_1 (
    .out0(decoder_1_out0), .out1(decoder_1_out1), .out2(decoder_1_out2), .out3(decoder_1_out3),
    .out4(decoder_1_out4), .out5(decoder_1_out5), .out6(decoder_1_out6), .out7(decoder_1_out7),
    .out8(decoder_1_out8), .out9(decoder_1_out9), .out10(decoder_1_out10), .out11(decoder_1_out11),
    .out12(decoder_1_out12), .out13(decoder_1_out13), .out14(decoder_1_out14), .out15(decoder_1_out15),
    .out16(decoder_1_out16), .out17(decoder_1_out17), .out18(decoder_1_out18), .out19(decoder_1_out19),
    .out20(decoder_1_out20), .out21(decoder_1_out21), .out22(decoder_1_out22), .out23(decoder_1_out23),
    .out24(decoder_1_out24), .out25(decoder_1_out25), .out26(decoder_1_out26), .out27(decoder_1_out27),
    .out28(decoder_1_out28), .out29(decoder_1_out29), .out30(decoder_1_out30), .out31(decoder_1_out31),
    .sel(Address), .en(Enable));
  D_Flip_Flop d_ff_1 (
    .clk(clock), .D(Input[3]), .Q(d_ff_97_q[3]), .en(decoder_1_out0), .reset(RESET));  // open: Qn, preset
  D_Flip_Flop d_ff_2 (
    .clk(clock), .D(Input[3]), .Q(d_ff_98_q[3]), .en(decoder_1_out1), .reset(RESET));  // open: Qn, preset
  D_Flip_Flop d_ff_3 (
    .clk(clock), .D(Input[3]), .Q(d_ff_99_q[3]), .en(decoder_1_out2), .reset(RESET));  // open: Qn, preset
  D_Flip_Flop d_ff_4 (
    .clk(clock), .D(Input[3]), .Q(d_ff_100_q[3]), .en(decoder_1_out3), .reset(RESET));  // open: Qn, preset
  D_Flip_Flop d_ff_5 (
    .clk(clock), .D(Input[3]), .Q(d_ff_101_q[3]), .en(decoder_1_out4), .reset(RESET));  // open: Qn, preset
  D_Flip_Flop d_ff_6 (
    .clk(clock), .D(Input[3]), .Q(d_ff_102_q[3]), .en(decoder_1_out5), .reset(RESET));  // open: Qn, preset
  D_Flip_Flop d_ff_7 (
    .clk(clock), .D(Input[3]), .Q(d_ff_103_q[3]), .en(decoder_1_out6), .reset(RESET));  // open: Qn, preset
  D_Flip_Flop d_ff_8 (
    .clk(clock), .D(Input[3]), .Q(d_ff_104_q[3]), .en(decoder_1_out7), .reset(RESET));  // open: Qn, preset
  D_Flip_Flop d_ff_9 (
    .clk(clock), .D(Input[3]), .Q(d_ff_105_q[3]), .en(decoder_1_out8), .reset(RESET));  // open: Qn, preset
  D_Flip_Flop d_ff_10 (
    .clk(clock), .D(Input[3]), .Q(d_ff_106_q[3]), .en(decoder_1_out9), .reset(RESET));  // open: Qn, preset
  D_Flip_Flop d_ff_11 (
    .clk(clock), .D(Input[3]), .Q(d_ff_107_q[3]), .en(decoder_1_out10), .reset(RESET));  // open: Qn, preset
  D_Flip_Flop d_ff_12 (
    .clk(clock), .D(Input[3]), .Q(d_ff_108_q[3]), .en(decoder_1_out11), .reset(RESET));  // open: Qn, preset
  D_Flip_Flop d_ff_13 (
    .clk(clock), .D(Input[3]), .Q(d_ff_109_q[3]), .en(decoder_1_out12), .reset(RESET));  // open: Qn, preset
  D_Flip_Flop d_ff_14 (
    .clk(clock), .D(Input[3]), .Q(d_ff_110_q[3]), .en(decoder_1_out13), .reset(RESET));  // open: Qn, preset
  D_Flip_Flop d_ff_15 (
    .clk(clock), .D(Input[3]), .Q(d_ff_111_q[3]), .en(decoder_1_out14), .reset(RESET));  // open: Qn, preset
  D_Flip_Flop d_ff_16 (
    .clk(clock), .D(Input[3]), .Q(d_ff_112_q[3]), .en(decoder_1_out15), .reset(RESET));  // open: Qn, preset
  D_Flip_Flop d_ff_17 (
    .clk(clock), .D(Input[3]), .Q(d_ff_113_q[3]), .en(decoder_1_out16), .reset(RESET));  // open: Qn, preset
  D_Flip_Flop d_ff_18 (
    .clk(clock), .D(Input[3]), .Q(d_ff_114_q[3]), .en(decoder_1_out17), .reset(RESET));  // open: Qn, preset
  D_Flip_Flop d_ff_19 (
    .clk(clock), .D(Input[3]), .Q(d_ff_115_q[3]), .en(decoder_1_out18), .reset(RESET));  // open: Qn, preset
  D_Flip_Flop d_ff_20 (
    .clk(clock), .D(Input[3]), .Q(d_ff_116_q[3]), .en(decoder_1_out19), .reset(RESET));  // open: Qn, preset
  D_Flip_Flop d_ff_21 (
    .clk(clock), .D(Input[3]), .Q(d_ff_117_q[3]), .en(decoder_1_out20), .reset(RESET));  // open: Qn, preset
  D_Flip_Flop d_ff_22 (
    .clk(clock), .D(Input[3]), .Q(d_ff_118_q[3]), .en(decoder_1_out21), .reset(RESET));  // open: Qn, preset
  D_Flip_Flop d_ff_23 (
    .clk(clock), .D(Input[3]), .Q(d_ff_119_q[3]), .en(decoder_1_out22), .reset(RESET));  // open: Qn, preset
  D_Flip_Flop d_ff_24 (
    .clk(clock), .D(Input[3]), .Q(d_ff_120_q[3]), .en(decoder_1_out23), .reset(RESET));  // open: Qn, preset
  D_Flip_Flop d_ff_25 (
    .clk(clock), .D(Input[3]), .Q(d_ff_121_q[3]), .en(decoder_1_out24), .reset(RESET));  // open: Qn, preset
  D_Flip_Flop d_ff_26 (
    .clk(clock), .D(Input[3]), .Q(d_ff_122_q[3]), .en(decoder_1_out25), .reset(RESET));  // open: Qn, preset
  D_Flip_Flop d_ff_27 (
    .clk(clock), .D(Input[3]), .Q(d_ff_123_q[3]), .en(decoder_1_out26), .reset(RESET));  // open: Qn, preset
  D_Flip_Flop d_ff_28 (
    .clk(clock), .D(Input[3]), .Q(d_ff_124_q[3]), .en(decoder_1_out27), .reset(RESET));  // open: Qn, preset
  D_Flip_Flop d_ff_29 (
    .clk(clock), .D(Input[3]), .Q(d_ff_125_q[3]), .en(decoder_1_out28), .reset(RESET));  // open: Qn, preset
  D_Flip_Flop d_ff_30 (
    .clk(clock), .D(Input[3]), .Q(d_ff_126_q[3]), .en(decoder_1_out29), .reset(RESET));  // open: Qn, preset
  D_Flip_Flop d_ff_31 (
    .clk(clock), .D(Input[3]), .Q(d_ff_127_q[3]), .en(decoder_1_out30), .reset(RESET));  // open: Qn, preset
  D_Flip_Flop d_ff_32 (
    .clk(clock), .D(Input[3]), .Q(d_ff_128_q[3]), .en(decoder_1_out31), .reset(RESET));  // open: Qn, preset
  D_Flip_Flop d_ff_33 (
    .clk(clock), .D(Input[2]), .Q(d_ff_97_q[2]), .en(decoder_1_out0), .reset(RESET));  // open: Qn, preset
  D_Flip_Flop d_ff_34 (
    .clk(clock), .D(Input[2]), .Q(d_ff_98_q[2]), .en(decoder_1_out1), .reset(RESET));  // open: Qn, preset
  D_Flip_Flop d_ff_35 (
    .clk(clock), .D(Input[2]), .Q(d_ff_99_q[2]), .en(decoder_1_out2), .reset(RESET));  // open: Qn, preset
  D_Flip_Flop d_ff_36 (
    .clk(clock), .D(Input[2]), .Q(d_ff_100_q[2]), .en(decoder_1_out3), .reset(RESET));  // open: Qn, preset
  D_Flip_Flop d_ff_37 (
    .clk(clock), .D(Input[2]), .Q(d_ff_101_q[2]), .en(decoder_1_out4), .reset(RESET));  // open: Qn, preset
  D_Flip_Flop d_ff_38 (
    .clk(clock), .D(Input[2]), .Q(d_ff_102_q[2]), .en(decoder_1_out5), .reset(RESET));  // open: Qn, preset
  D_Flip_Flop d_ff_39 (
    .clk(clock), .D(Input[2]), .Q(d_ff_103_q[2]), .en(decoder_1_out6), .reset(RESET));  // open: Qn, preset
  D_Flip_Flop d_ff_40 (
    .clk(clock), .D(Input[2]), .Q(d_ff_104_q[2]), .en(decoder_1_out7), .reset(RESET));  // open: Qn, preset
  D_Flip_Flop d_ff_41 (
    .clk(clock), .D(Input[2]), .Q(d_ff_105_q[2]), .en(decoder_1_out8), .reset(RESET));  // open: Qn, preset
  D_Flip_Flop d_ff_42 (
    .clk(clock), .D(Input[2]), .Q(d_ff_106_q[2]), .en(decoder_1_out9), .reset(RESET));  // open: Qn, preset
  D_Flip_Flop d_ff_43 (
    .clk(clock), .D(Input[2]), .Q(d_ff_107_q[2]), .en(decoder_1_out10), .reset(RESET));  // open: Qn, preset
  D_Flip_Flop d_ff_44 (
    .clk(clock), .D(Input[2]), .Q(d_ff_108_q[2]), .en(decoder_1_out11), .reset(RESET));  // open: Qn, preset
  D_Flip_Flop d_ff_45 (
    .clk(clock), .D(Input[2]), .Q(d_ff_109_q[2]), .en(decoder_1_out12), .reset(RESET));  // open: Qn, preset
  D_Flip_Flop d_ff_46 (
    .clk(clock), .D(Input[2]), .Q(d_ff_110_q[2]), .en(decoder_1_out13), .reset(RESET));  // open: Qn, preset
  D_Flip_Flop d_ff_47 (
    .clk(clock), .D(Input[2]), .Q(d_ff_111_q[2]), .en(decoder_1_out14), .reset(RESET));  // open: Qn, preset
  D_Flip_Flop d_ff_48 (
    .clk(clock), .D(Input[2]), .Q(d_ff_112_q[2]), .en(decoder_1_out15), .reset(RESET));  // open: Qn, preset
  D_Flip_Flop d_ff_49 (
    .clk(clock), .D(Input[2]), .Q(d_ff_113_q[2]), .en(decoder_1_out16), .reset(RESET));  // open: Qn, preset
  D_Flip_Flop d_ff_50 (
    .clk(clock), .D(Input[2]), .Q(d_ff_114_q[2]), .en(decoder_1_out17), .reset(RESET));  // open: Qn, preset
  D_Flip_Flop d_ff_51 (
    .clk(clock), .D(Input[2]), .Q(d_ff_115_q[2]), .en(decoder_1_out18), .reset(RESET));  // open: Qn, preset
  D_Flip_Flop d_ff_52 (
    .clk(clock), .D(Input[2]), .Q(d_ff_116_q[2]), .en(decoder_1_out19), .reset(RESET));  // open: Qn, preset
  D_Flip_Flop d_ff_53 (
    .clk(clock), .D(Input[2]), .Q(d_ff_117_q[2]), .en(decoder_1_out20), .reset(RESET));  // open: Qn, preset
  D_Flip_Flop d_ff_54 (
    .clk(clock), .D(Input[2]), .Q(d_ff_118_q[2]), .en(decoder_1_out21), .reset(RESET));  // open: Qn, preset
  D_Flip_Flop d_ff_55 (
    .clk(clock), .D(Input[2]), .Q(d_ff_119_q[2]), .en(decoder_1_out22), .reset(RESET));  // open: Qn, preset
  D_Flip_Flop d_ff_56 (
    .clk(clock), .D(Input[2]), .Q(d_ff_120_q[2]), .en(decoder_1_out23), .reset(RESET));  // open: Qn, preset
  D_Flip_Flop d_ff_57 (
    .clk(clock), .D(Input[2]), .Q(d_ff_121_q[2]), .en(decoder_1_out24), .reset(RESET));  // open: Qn, preset
  D_Flip_Flop d_ff_58 (
    .clk(clock), .D(Input[2]), .Q(d_ff_122_q[2]), .en(decoder_1_out25), .reset(RESET));  // open: Qn, preset
  D_Flip_Flop d_ff_59 (
    .clk(clock), .D(Input[2]), .Q(d_ff_123_q[2]), .en(decoder_1_out26), .reset(RESET));  // open: Qn, preset
  D_Flip_Flop d_ff_60 (
    .clk(clock), .D(Input[2]), .Q(d_ff_124_q[2]), .en(decoder_1_out27), .reset(RESET));  // open: Qn, preset
  D_Flip_Flop d_ff_61 (
    .clk(clock), .D(Input[2]), .Q(d_ff_125_q[2]), .en(decoder_1_out28), .reset(RESET));  // open: Qn, preset
  D_Flip_Flop d_ff_62 (
    .clk(clock), .D(Input[2]), .Q(d_ff_126_q[2]), .en(decoder_1_out29), .reset(RESET));  // open: Qn, preset
  D_Flip_Flop d_ff_63 (
    .clk(clock), .D(Input[2]), .Q(d_ff_127_q[2]), .en(decoder_1_out30), .reset(RESET));  // open: Qn, preset
  D_Flip_Flop d_ff_64 (
    .clk(clock), .D(Input[2]), .Q(d_ff_128_q[2]), .en(decoder_1_out31), .reset(RESET));  // open: Qn, preset
  D_Flip_Flop d_ff_65 (
    .clk(clock), .D(Input[1]), .Q(d_ff_97_q[1]), .en(decoder_1_out0), .reset(RESET));  // open: Qn, preset
  D_Flip_Flop d_ff_66 (
    .clk(clock), .D(Input[1]), .Q(d_ff_98_q[1]), .en(decoder_1_out1), .reset(RESET));  // open: Qn, preset
  D_Flip_Flop d_ff_67 (
    .clk(clock), .D(Input[1]), .Q(d_ff_99_q[1]), .en(decoder_1_out2), .reset(RESET));  // open: Qn, preset
  D_Flip_Flop d_ff_68 (
    .clk(clock), .D(Input[1]), .Q(d_ff_100_q[1]), .en(decoder_1_out3), .reset(RESET));  // open: Qn, preset
  D_Flip_Flop d_ff_69 (
    .clk(clock), .D(Input[1]), .Q(d_ff_101_q[1]), .en(decoder_1_out4), .reset(RESET));  // open: Qn, preset
  D_Flip_Flop d_ff_70 (
    .clk(clock), .D(Input[1]), .Q(d_ff_102_q[1]), .en(decoder_1_out5), .reset(RESET));  // open: Qn, preset
  D_Flip_Flop d_ff_71 (
    .clk(clock), .D(Input[1]), .Q(d_ff_103_q[1]), .en(decoder_1_out6), .reset(RESET));  // open: Qn, preset
  D_Flip_Flop d_ff_72 (
    .clk(clock), .D(Input[1]), .Q(d_ff_104_q[1]), .en(decoder_1_out7), .reset(RESET));  // open: Qn, preset
  D_Flip_Flop d_ff_73 (
    .clk(clock), .D(Input[1]), .Q(d_ff_105_q[1]), .en(decoder_1_out8), .reset(RESET));  // open: Qn, preset
  D_Flip_Flop d_ff_74 (
    .clk(clock), .D(Input[1]), .Q(d_ff_106_q[1]), .en(decoder_1_out9), .reset(RESET));  // open: Qn, preset
  D_Flip_Flop d_ff_75 (
    .clk(clock), .D(Input[1]), .Q(d_ff_107_q[1]), .en(decoder_1_out10), .reset(RESET));  // open: Qn, preset
  D_Flip_Flop d_ff_76 (
    .clk(clock), .D(Input[1]), .Q(d_ff_108_q[1]), .en(decoder_1_out11), .reset(RESET));  // open: Qn, preset
  D_Flip_Flop d_ff_77 (
    .clk(clock), .D(Input[1]), .Q(d_ff_109_q[1]), .en(decoder_1_out12), .reset(RESET));  // open: Qn, preset
  D_Flip_Flop d_ff_78 (
    .clk(clock), .D(Input[1]), .Q(d_ff_110_q[1]), .en(decoder_1_out13), .reset(RESET));  // open: Qn, preset
  D_Flip_Flop d_ff_79 (
    .clk(clock), .D(Input[1]), .Q(d_ff_111_q[1]), .en(decoder_1_out14), .reset(RESET));  // open: Qn, preset
  D_Flip_Flop d_ff_80 (
    .clk(clock), .D(Input[1]), .Q(d_ff_112_q[1]), .en(decoder_1_out15), .reset(RESET));  // open: Qn, preset
  D_Flip_Flop d_ff_81 (
    .clk(clock), .D(Input[1]), .Q(d_ff_113_q[1]), .en(decoder_1_out16), .reset(RESET));  // open: Qn, preset
  D_Flip_Flop d_ff_82 (
    .clk(clock), .D(Input[1]), .Q(d_ff_114_q[1]), .en(decoder_1_out17), .reset(RESET));  // open: Qn, preset
  D_Flip_Flop d_ff_83 (
    .clk(clock), .D(Input[1]), .Q(d_ff_115_q[1]), .en(decoder_1_out18), .reset(RESET));  // open: Qn, preset
  D_Flip_Flop d_ff_84 (
    .clk(clock), .D(Input[1]), .Q(d_ff_116_q[1]), .en(decoder_1_out19), .reset(RESET));  // open: Qn, preset
  D_Flip_Flop d_ff_85 (
    .clk(clock), .D(Input[1]), .Q(d_ff_117_q[1]), .en(decoder_1_out20), .reset(RESET));  // open: Qn, preset
  D_Flip_Flop d_ff_86 (
    .clk(clock), .D(Input[1]), .Q(d_ff_118_q[1]), .en(decoder_1_out21), .reset(RESET));  // open: Qn, preset
  D_Flip_Flop d_ff_87 (
    .clk(clock), .D(Input[1]), .Q(d_ff_119_q[1]), .en(decoder_1_out22), .reset(RESET));  // open: Qn, preset
  D_Flip_Flop d_ff_88 (
    .clk(clock), .D(Input[1]), .Q(d_ff_120_q[1]), .en(decoder_1_out23), .reset(RESET));  // open: Qn, preset
  D_Flip_Flop d_ff_89 (
    .clk(clock), .D(Input[1]), .Q(d_ff_121_q[1]), .en(decoder_1_out24), .reset(RESET));  // open: Qn, preset
  D_Flip_Flop d_ff_90 (
    .clk(clock), .D(Input[1]), .Q(d_ff_122_q[1]), .en(decoder_1_out25), .reset(RESET));  // open: Qn, preset
  D_Flip_Flop d_ff_91 (
    .clk(clock), .D(Input[1]), .Q(d_ff_123_q[1]), .en(decoder_1_out26), .reset(RESET));  // open: Qn, preset
  D_Flip_Flop d_ff_92 (
    .clk(clock), .D(Input[1]), .Q(d_ff_124_q[1]), .en(decoder_1_out27), .reset(RESET));  // open: Qn, preset
  D_Flip_Flop d_ff_93 (
    .clk(clock), .D(Input[1]), .Q(d_ff_125_q[1]), .en(decoder_1_out28), .reset(RESET));  // open: Qn, preset
  D_Flip_Flop d_ff_94 (
    .clk(clock), .D(Input[1]), .Q(d_ff_126_q[1]), .en(decoder_1_out29), .reset(RESET));  // open: Qn, preset
  D_Flip_Flop d_ff_95 (
    .clk(clock), .D(Input[1]), .Q(d_ff_127_q[1]), .en(decoder_1_out30), .reset(RESET));  // open: Qn, preset
  D_Flip_Flop d_ff_96 (
    .clk(clock), .D(Input[1]), .Q(d_ff_128_q[1]), .en(decoder_1_out31), .reset(RESET));  // open: Qn, preset
  D_Flip_Flop d_ff_97 (
    .clk(clock), .D(Input[0]), .Q(d_ff_97_q[0]), .en(decoder_1_out0), .reset(RESET));  // open: Qn, preset
  D_Flip_Flop d_ff_98 (
    .clk(clock), .D(Input[0]), .Q(d_ff_98_q[0]), .en(decoder_1_out1), .reset(RESET));  // open: Qn, preset
  D_Flip_Flop d_ff_99 (
    .clk(clock), .D(Input[0]), .Q(d_ff_99_q[0]), .en(decoder_1_out2), .reset(RESET));  // open: Qn, preset
  D_Flip_Flop d_ff_100 (
    .clk(clock), .D(Input[0]), .Q(d_ff_100_q[0]), .en(decoder_1_out3), .reset(RESET));  // open: Qn, preset
  D_Flip_Flop d_ff_101 (
    .clk(clock), .D(Input[0]), .Q(d_ff_101_q[0]), .en(decoder_1_out4), .reset(RESET));  // open: Qn, preset
  D_Flip_Flop d_ff_102 (
    .clk(clock), .D(Input[0]), .Q(d_ff_102_q[0]), .en(decoder_1_out5), .reset(RESET));  // open: Qn, preset
  D_Flip_Flop d_ff_103 (
    .clk(clock), .D(Input[0]), .Q(d_ff_103_q[0]), .en(decoder_1_out6), .reset(RESET));  // open: Qn, preset
  D_Flip_Flop d_ff_104 (
    .clk(clock), .D(Input[0]), .Q(d_ff_104_q[0]), .en(decoder_1_out7), .reset(RESET));  // open: Qn, preset
  D_Flip_Flop d_ff_105 (
    .clk(clock), .D(Input[0]), .Q(d_ff_105_q[0]), .en(decoder_1_out8), .reset(RESET));  // open: Qn, preset
  D_Flip_Flop d_ff_106 (
    .clk(clock), .D(Input[0]), .Q(d_ff_106_q[0]), .en(decoder_1_out9), .reset(RESET));  // open: Qn, preset
  D_Flip_Flop d_ff_107 (
    .clk(clock), .D(Input[0]), .Q(d_ff_107_q[0]), .en(decoder_1_out10), .reset(RESET));  // open: Qn, preset
  D_Flip_Flop d_ff_108 (
    .clk(clock), .D(Input[0]), .Q(d_ff_108_q[0]), .en(decoder_1_out11), .reset(RESET));  // open: Qn, preset
  D_Flip_Flop d_ff_109 (
    .clk(clock), .D(Input[0]), .Q(d_ff_109_q[0]), .en(decoder_1_out12), .reset(RESET));  // open: Qn, preset
  D_Flip_Flop d_ff_110 (
    .clk(clock), .D(Input[0]), .Q(d_ff_110_q[0]), .en(decoder_1_out13), .reset(RESET));  // open: Qn, preset
  D_Flip_Flop d_ff_111 (
    .clk(clock), .D(Input[0]), .Q(d_ff_111_q[0]), .en(decoder_1_out14), .reset(RESET));  // open: Qn, preset
  D_Flip_Flop d_ff_112 (
    .clk(clock), .D(Input[0]), .Q(d_ff_112_q[0]), .en(decoder_1_out15), .reset(RESET));  // open: Qn, preset
  D_Flip_Flop d_ff_113 (
    .clk(clock), .D(Input[0]), .Q(d_ff_113_q[0]), .en(decoder_1_out16), .reset(RESET));  // open: Qn, preset
  D_Flip_Flop d_ff_114 (
    .clk(clock), .D(Input[0]), .Q(d_ff_114_q[0]), .en(decoder_1_out17), .reset(RESET));  // open: Qn, preset
  D_Flip_Flop d_ff_115 (
    .clk(clock), .D(Input[0]), .Q(d_ff_115_q[0]), .en(decoder_1_out18), .reset(RESET));  // open: Qn, preset
  D_Flip_Flop d_ff_116 (
    .clk(clock), .D(Input[0]), .Q(d_ff_116_q[0]), .en(decoder_1_out19), .reset(RESET));  // open: Qn, preset
  D_Flip_Flop d_ff_117 (
    .clk(clock), .D(Input[0]), .Q(d_ff_117_q[0]), .en(decoder_1_out20), .reset(RESET));  // open: Qn, preset
  D_Flip_Flop d_ff_118 (
    .clk(clock), .D(Input[0]), .Q(d_ff_118_q[0]), .en(decoder_1_out21), .reset(RESET));  // open: Qn, preset
  D_Flip_Flop d_ff_119 (
    .clk(clock), .D(Input[0]), .Q(d_ff_119_q[0]), .en(decoder_1_out22), .reset(RESET));  // open: Qn, preset
  D_Flip_Flop d_ff_120 (
    .clk(clock), .D(Input[0]), .Q(d_ff_120_q[0]), .en(decoder_1_out23), .reset(RESET));  // open: Qn, preset
  D_Flip_Flop d_ff_121 (
    .clk(clock), .D(Input[0]), .Q(d_ff_121_q[0]), .en(decoder_1_out24), .reset(RESET));  // open: Qn, preset
  D_Flip_Flop d_ff_122 (
    .clk(clock), .D(Input[0]), .Q(d_ff_122_q[0]), .en(decoder_1_out25), .reset(RESET));  // open: Qn, preset
  D_Flip_Flop d_ff_123 (
    .clk(clock), .D(Input[0]), .Q(d_ff_123_q[0]), .en(decoder_1_out26), .reset(RESET));  // open: Qn, preset
  D_Flip_Flop d_ff_124 (
    .clk(clock), .D(Input[0]), .Q(d_ff_124_q[0]), .en(decoder_1_out27), .reset(RESET));  // open: Qn, preset
  D_Flip_Flop d_ff_125 (
    .clk(clock), .D(Input[0]), .Q(d_ff_125_q[0]), .en(decoder_1_out28), .reset(RESET));  // open: Qn, preset
  D_Flip_Flop d_ff_126 (
    .clk(clock), .D(Input[0]), .Q(d_ff_126_q[0]), .en(decoder_1_out29), .reset(RESET));  // open: Qn, preset
  D_Flip_Flop d_ff_127 (
    .clk(clock), .D(Input[0]), .Q(d_ff_127_q[0]), .en(decoder_1_out30), .reset(RESET));  // open: Qn, preset
  D_Flip_Flop d_ff_128 (
    .clk(clock), .D(Input[0]), .Q(d_ff_128_q[0]), .en(decoder_1_out31), .reset(RESET));  // open: Qn, preset
  Multiplexer #(.select(5), .width(4)) multiplexer_1 (
    .in0(d_ff_97_q), .in1(d_ff_98_q), .in2(d_ff_99_q), .in3(d_ff_100_q), .in4(d_ff_101_q), .in5(d_ff_102_q),
    .in6(d_ff_103_q), .in7(d_ff_104_q), .in8(d_ff_105_q), .in9(d_ff_106_q), .in10(d_ff_107_q),
    .in11(d_ff_108_q), .in12(d_ff_109_q), .in13(d_ff_110_q), .in14(d_ff_111_q), .in15(d_ff_112_q),
    .in16(d_ff_113_q), .in17(d_ff_114_q), .in18(d_ff_115_q), .in19(d_ff_116_q), .in20(d_ff_117_q),
    .in21(d_ff_118_q), .in22(d_ff_119_q), .in23(d_ff_120_q), .in24(d_ff_121_q), .in25(d_ff_122_q),
    .in26(d_ff_123_q), .in27(undriven), .in28(d_ff_125_q), .in29(d_ff_126_q), .in30(d_ff_127_q),
    .in31(d_ff_128_q), .out(Output), .sel(Address));  // open: en

  // Notes on the sheet:
  //   5 bit address
  //   location to store data
endmodule
